# Fritzing sketch motoren (saved by Fritzing 0.9.3b)
breadboards: 1

parts:
  IC1 = L293D [package=THT]
  IC2 = L293D [package=THT]
  M1 = DC Motor
  M2 = DC Motor
  M3 = DC Motor
  M4 = DC Motor

nets:
  N1: IC1.Enable_1, IC1.+Vmotor, IC1.Enable_2, IC1.+V, IC2.Enable_1, IC2.+Vmotor, IC2.Enable_2, IC2.+V
  N2: IC1.Out_1_(_Controlled_by_Enable_1_), M4.pin_2
  N3: IC1.0V, IC2.0V
  N4: IC1.Out_2_(_Controlled_by_Enable_1_), M4.pin_1
  N5: IC1.Out_3_(_Controlled_by_Enable_2_), M3.pin_2
  N6: IC1.Out_4_(_Controlled_by_Enable_2_), M3.pin_1
  N7: IC2.Out_1_(_Controlled_by_Enable_1_), M1.pin_2
  N8: IC2.Out_2_(_Controlled_by_Enable_1_), M1.pin_1
  N9: IC2.Out_3_(_Controlled_by_Enable_2_), M2.pin_2
  N10: IC2.Out_4_(_Controlled_by_Enable_2_), M2.pin_1
